// Logisim project d8421+6.circ as structural Verilog: 1 circuit, main circuit main
module main (
  input  [3:0] in_1,
  output [3:0] out_2,
  output [3:0] out_3,
  output [3:0] out_4
);

  wire and_1_out, and_2_out;

  not not_1 (out_3[1], in_1[1]);
  or or_1 (out_3[3], in_1[3], in_1[1], in_1[2]);
  and and_1 (and_1_out, ~in_1[3], in_1[1], in_1[2]);  // AND_Gate
  and and_2 (and_2_out, ~in_1[1], ~in_1[2]);  // AND_Gate
  or or_2 (out_3[2], and_1_out, and_2_out);

  assign out_2 = in_1;
  assign out_3[0] = in_1[0];
  assign out_4 = {out_3[3:1], in_1[0]};

  // Notes on the sheet:
  //   Y2
  //   Y1
endmodule
